# Fritzing sketch chdk-arduino (saved by Fritzing 0.7.1b)
breadboards: 1

parts:
  Arduino1 = Arduino
  S1 = Pushbutton [package="[THT]"]
  R4 = 10k Ω Resistor [package=THT]
  R2 = 10k Ω Resistor [package=THT]
  R3 = 10k Ω Resistor [package=THT]
  R1 = Basic Photo-Resistor (Photocell) [package=THT]
  USB_CHDK = USB connector [package=THT]

nets:
  GND: Arduino1.GND, S1.Pin_1, S1.Pin_2, R2.Pin_0, USB_CHDK.GND, USB_CHDK.chassis5, USB_CHDK.chassis6
  N1: Arduino1.D13, USB_CHDK.5V
  N2: Arduino1.D7, S1.Pin_3, S1.Pin_4, R4.Pin_1
  N3: Arduino1.+5V, R4.Pin_0, R1.pin_1
  N4: Arduino1.A0, R3.Pin_0, R1.pin_0
  N5: R2.Pin_1, R3.Pin_1
